# Fritzing sketch Sensing Temperature-3LED (saved by Fritzing 0.9.3b)
breadboards: 1

parts:
  Part1 = Arduino Uno (Rev3)
  R2 = Resistor [tolerance=±5% resistance=1k package="0805 [SMD]"]
  R1 = Temperature Sensor (Thermistor) [thermistor_type=NTC package=THT]
  LED1 = RGB LED (com. cathode, rbg) [package="5 mm [THT]"]
  R3 = Resistor [tolerance=±5% resistance=330 package="0805 [SMD]"]

nets:
  N1: Part1.A0, R2.Pin_0, R1.pin_0
  N2: Part1.D3_PWM, LED1.green_anode
  N3: Part1.D4, LED1.blue_anode
  N4: Part1.D5_PWM, LED1.red_anode
  N5: Part1.5V, R1.pin_1
  N6: Part1.GND, R2.Pin_1, R3.Pin_0
  N7: LED1.common_cathode, R3.Pin_1

notes:
  Sensing Temperature - RGB LED
  Changes in temperature affect the color of the LED
